// Logisim project cpu.circ as structural Verilog
module main (
);

  wire [31:0] alu_result, extender_out_2, multiplexer_1_out, multiplexer_2_out, ram_1_data, reg_rdata1,
       reg_rdata2;
  wire [31:5] undriven;

  Clock clock_1 ();  // open: out
  IFU ifu_1 ();
  // Probe on {undriven[31:11], {5{undriven[11]}}, {6{undriven[5]}}}
  // Probe on undriven[5]
  // Probe on undriven[11]
  Control controller ();
  RegFile \reg  (
    .wdata(multiplexer_2_out), .Rdata1(reg_rdata1), .Rdata2(reg_rdata2));  // open: reg1, wreg, regwrite, reg2
  Extender extender (.out_2(extender_out_2));  // open: in_1
  Multiplexer #(.width(32)) multiplexer_1 (
    .in0(reg_rdata2), .in1(extender_out_2), .out(multiplexer_1_out));  // open: sel, en
  ALU alu (.A(reg_rdata1), .B(multiplexer_1_out), .result(alu_result));
  Multiplexer #(.width(32)) multiplexer_2 (
    .in0(ram_1_data), .in1(alu_result), .out(multiplexer_2_out));  // open: sel, en
  RAM #(.addrWidth(6), .dataWidth(32), .bus("separate")) ram_1 (
    .addr({alu_result[20], alu_result[16], alu_result[12], alu_result[8], alu_result[4], alu_result[0]}),
    .din(reg_rdata2), .data(ram_1_data));  // open: str, sel, clk, ld, clr
  // Pins of 1 and 4 bits meet at alu_result[3:0]
  // Pins of 1 and 4 bits meet at alu_result[7:4]
  // Pins of 1 and 4 bits meet at alu_result[11:8]
  // Pins of 1 and 4 bits meet at alu_result[15:12]
  // Pins of 1 and 4 bits meet at alu_result[19:16]
  // Pins of 1 and 4 bits meet at alu_result[23:20]
endmodule

module RegFile (
  input  [4:0] reg1,
  input  [4:0] wreg,
  input  regwrite,
  input  [31:0] wdata,
  input  [4:0] reg2,
  output [31:0] Rdata1,
  output [31:0] Rdata2
);

  wire and_1_out, and_2_out, and_3_out, and_4_out, and_5_out, and_6_out, and_7_out, and_8_out, and_9_out,
       and_10_out, and_11_out, and_12_out, and_13_out, and_14_out, and_15_out, and_16_out, and_17_out,
       and_18_out, and_19_out, and_20_out, and_21_out, and_22_out, and_23_out, and_24_out, and_25_out,
       and_26_out, and_27_out, and_28_out, and_29_out, and_30_out, and_31_out, and_32_out, clock_1_out,
       decoder_1_out0, decoder_1_out1, decoder_1_out2, decoder_1_out3, decoder_1_out4, decoder_1_out5,
       decoder_1_out6, decoder_1_out7, decoder_1_out8, decoder_1_out9, decoder_1_out10, decoder_1_out11,
       decoder_1_out12, decoder_1_out13, decoder_1_out14, decoder_1_out15, decoder_1_out16, decoder_1_out17,
       decoder_1_out18, decoder_1_out19, decoder_1_out20, decoder_1_out21, decoder_1_out22, decoder_1_out23,
       decoder_1_out24, decoder_1_out25, decoder_1_out26, decoder_1_out27, decoder_1_out28, decoder_1_out29,
       decoder_1_out30, decoder_1_out31;
  wire [31:0] reg0_q, reg1_q, reg2_q, reg3_q, reg4_q, reg5_q, reg6_q, reg7_q, reg8_q, reg9_q, reg10_q,
       reg11_q, reg12_q, reg13_q, reg14_q, reg15_q, reg16_q, reg17_q, reg18_q, reg19_q, reg20_q, reg21_q,
       reg22_q, reg23_q, reg24_q, reg25_q, reg26_q, reg27_q, reg28_q, reg29_q, reg30_q, reg31_q;

  Clock clock_1 (.out(clock_1_out));
  Decoder #(.select(5), .enable("false")) decoder_1 (
    .out0(decoder_1_out0), .out1(decoder_1_out1), .out2(decoder_1_out2), .out3(decoder_1_out3),
    .out4(decoder_1_out4), .out5(decoder_1_out5), .out6(decoder_1_out6), .out7(decoder_1_out7),
    .out8(decoder_1_out8), .out9(decoder_1_out9), .out10(decoder_1_out10), .out11(decoder_1_out11),
    .out12(decoder_1_out12), .out13(decoder_1_out13), .out14(decoder_1_out14), .out15(decoder_1_out15),
    .out16(decoder_1_out16), .out17(decoder_1_out17), .out18(decoder_1_out18), .out19(decoder_1_out19),
    .out20(decoder_1_out20), .out21(decoder_1_out21), .out22(decoder_1_out22), .out23(decoder_1_out23),
    .out24(decoder_1_out24), .out25(decoder_1_out25), .out26(decoder_1_out26), .out27(decoder_1_out27),
    .out28(decoder_1_out28), .out29(decoder_1_out29), .out30(decoder_1_out30), .out31(decoder_1_out31),
    .sel(wreg));
  and and_1 (and_1_out, decoder_1_out1, clock_1_out);
  and and_2 (and_2_out, decoder_1_out2, clock_1_out, regwrite);
  and and_3 (and_3_out, decoder_1_out3, clock_1_out, regwrite);
  and and_4 (and_4_out, decoder_1_out4, clock_1_out, regwrite);
  and and_5 (and_5_out, decoder_1_out5, clock_1_out, regwrite);
  and and_6 (and_6_out, decoder_1_out6, clock_1_out, regwrite);
  and and_7 (and_7_out, decoder_1_out7, clock_1_out, regwrite);
  and and_8 (and_8_out, decoder_1_out8, clock_1_out, regwrite);
  and and_9 (and_9_out, decoder_1_out9, clock_1_out, regwrite);
  and and_10 (and_10_out, decoder_1_out10, clock_1_out, regwrite);
  and and_11 (and_11_out, decoder_1_out11, clock_1_out, regwrite);
  and and_12 (and_12_out, decoder_1_out12, clock_1_out, regwrite);
  and and_13 (and_13_out, decoder_1_out13, clock_1_out, regwrite);
  and and_14 (and_14_out, decoder_1_out14, clock_1_out, regwrite);
  and and_15 (and_15_out, decoder_1_out15, clock_1_out, regwrite);
  and and_16 (and_16_out, decoder_1_out16, clock_1_out, regwrite);
  and and_17 (and_17_out, decoder_1_out17, clock_1_out, regwrite);
  and and_18 (and_18_out, decoder_1_out18, clock_1_out, regwrite);
  and and_19 (and_19_out, decoder_1_out19, clock_1_out, regwrite);
  and and_20 (and_20_out, decoder_1_out20, clock_1_out, regwrite);
  and and_21 (and_21_out, decoder_1_out21, clock_1_out, regwrite);
  and and_22 (and_22_out, decoder_1_out22, clock_1_out, regwrite);
  and and_23 (and_23_out, decoder_1_out23, clock_1_out, regwrite);
  and and_24 (and_24_out, decoder_1_out24, clock_1_out, regwrite);
  and and_25 (and_25_out, decoder_1_out25, clock_1_out, regwrite);
  and and_26 (and_26_out, decoder_1_out26, clock_1_out, regwrite);
  and and_27 (and_27_out, decoder_1_out27, clock_1_out, regwrite);
  and and_28 (and_28_out, decoder_1_out28, clock_1_out, regwrite);
  and and_29 (and_29_out, decoder_1_out29, clock_1_out, regwrite);
  and and_30 (and_30_out, decoder_1_out30, clock_1_out, regwrite);
  and and_31 (and_31_out, decoder_1_out31, clock_1_out, regwrite);
  and and_32 (and_32_out, decoder_1_out0, clock_1_out, regwrite);
  Register #(.width(32)) reg0 (.D(wdata), .Q(reg0_q), .clk(and_32_out));  // open: en, clr
  Register #(.width(32)) u_reg2 (.D(wdata), .Q(reg2_q), .clk(and_2_out));  // open: en, clr
  Register #(.width(32)) reg4 (.D(wdata), .Q(reg4_q), .clk(and_4_out));  // open: en, clr
  Register #(.width(32)) reg6 (.D(wdata), .Q(reg6_q), .clk(and_6_out));  // open: en, clr
  Register #(.width(32)) reg8 (.D(wdata), .Q(reg8_q), .clk(and_8_out));  // open: en, clr
  Register #(.width(32)) reg10 (.D(wdata), .Q(reg10_q), .clk(and_10_out));  // open: en, clr
  Register #(.width(32)) reg12 (.D(wdata), .Q(reg12_q), .clk(and_12_out));  // open: en, clr
  Register #(.width(32)) reg14 (.D(wdata), .Q(reg14_q), .clk(and_14_out));  // open: en, clr
  Register #(.width(32)) reg16 (.D(wdata), .Q(reg16_q), .clk(and_16_out));  // open: en, clr
  Register #(.width(32)) reg18 (.D(wdata), .Q(reg18_q), .clk(and_18_out));  // open: en, clr
  Register #(.width(32)) reg20 (.D(wdata), .Q(reg20_q), .clk(and_20_out));  // open: en, clr
  Register #(.width(32)) reg22 (.D(wdata), .Q(reg22_q), .clk(and_22_out));  // open: en, clr
  Register #(.width(32)) reg24 (.D(wdata), .Q(reg24_q), .clk(and_24_out));  // open: en, clr
  Register #(.width(32)) reg26 (.D(wdata), .Q(reg26_q), .clk(and_26_out));  // open: en, clr
  Register #(.width(32)) reg28 (.D(wdata), .Q(reg28_q), .clk(and_28_out));  // open: en, clr
  Register #(.width(32)) reg30 (.D(wdata), .Q(reg30_q), .clk(and_30_out));  // open: en, clr
  Register #(.width(32)) u_reg1 (.D(wdata), .Q(reg1_q), .clk(and_1_out));  // open: en, clr
  Register #(.width(32)) reg3 (.D(wdata), .Q(reg3_q), .clk(and_3_out));  // open: en, clr
  Register #(.width(32)) reg5 (.D(wdata), .Q(reg5_q), .clk(and_5_out));  // open: en, clr
  Register #(.width(32)) reg7 (.D(wdata), .Q(reg7_q), .clk(and_7_out));  // open: en, clr
  Register #(.width(32)) reg9 (.D(wdata), .Q(reg9_q), .clk(and_9_out));  // open: en, clr
  Register #(.width(32)) reg11 (.D(wdata), .Q(reg11_q), .clk(and_11_out));  // open: en, clr
  Register #(.width(32)) reg13 (.D(wdata), .Q(reg13_q), .clk(and_13_out));  // open: en, clr
  Register #(.width(32)) reg15 (.D(wdata), .Q(reg15_q), .clk(and_15_out));  // open: en, clr
  Register #(.width(32)) reg17 (.D(wdata), .Q(reg17_q), .clk(and_17_out));  // open: en, clr
  Register #(.width(32)) reg19 (.D(wdata), .Q(reg19_q), .clk(and_19_out));  // open: en, clr
  Register #(.width(32)) reg21 (.D(wdata), .Q(reg21_q), .clk(and_21_out));  // open: en, clr
  Register #(.width(32)) reg23 (.D(wdata), .Q(reg23_q), .clk(and_23_out));  // open: en, clr
  Register #(.width(32)) reg25 (.D(wdata), .Q(reg25_q), .clk(and_25_out));  // open: en, clr
  Register #(.width(32)) reg27 (.D(wdata), .Q(reg27_q), .clk(and_27_out));  // open: en, clr
  Register #(.width(32)) reg29 (.D(wdata), .Q(reg29_q), .clk(and_29_out));  // open: en, clr
  Register #(.width(32)) reg31 (.D(wdata), .Q(reg31_q), .clk(and_31_out));  // open: en, clr
  Multiplexer #(.select(5), .width(32)) multiplexer_1 (
    .in0(reg0_q), .in1(reg1_q), .in2(reg2_q), .in3(reg3_q), .in4(reg4_q), .in5(reg5_q), .in6(reg6_q),
    .in7(reg7_q), .in8(reg8_q), .in9(reg9_q), .in10(reg10_q), .in11(reg11_q), .in12(reg12_q), .in13(reg13_q),
    .in14(reg14_q), .in15(reg15_q), .in16(reg16_q), .in17(reg17_q), .in18(reg18_q), .in19(reg19_q),
    .in20(reg20_q), .in21(reg21_q), .in22(reg22_q), .in23(reg23_q), .in24(reg24_q), .in25(reg25_q),
    .in26(reg26_q), .in27(reg27_q), .in28(reg28_q), .in29(reg29_q), .in30(reg30_q), .in31(reg31_q),
    .out(Rdata1), .sel(reg1));  // open: en
  Multiplexer #(.select(5), .width(32)) multiplexer_2 (
    .in0(reg0_q), .in1(reg1_q), .in2(reg2_q), .in3(reg3_q), .in4(reg4_q), .in5(reg5_q), .in6(reg6_q),
    .in7(reg7_q), .in8(reg8_q), .in9(reg9_q), .in10(reg10_q), .in11(reg11_q), .in12(reg12_q), .in13(reg13_q),
    .in14(reg14_q), .in15(reg15_q), .in16(reg16_q), .in17(reg17_q), .in18(reg18_q), .in19(reg19_q),
    .in20(reg20_q), .in21(reg21_q), .in22(reg22_q), .in23(reg23_q), .in24(reg24_q), .in25(reg25_q),
    .in26(reg26_q), .in27(reg27_q), .in28(reg28_q), .in29(reg29_q), .in30(reg30_q), .in31(reg31_q),
    .out(Rdata2), .sel(reg2));  // open: en
endmodule

module ALU (
  input  [31:0] A,
  input  [31:0] B,
  output [31:0] result
);

  Adder #(.width(32)) adder_1 (.a(A), .b(B), .out(result));  // open: cin, cout
endmodule

module IFU (
);

  Clock clock_1 ();  // open: out
  ROM #(.addrWidth(4), .dataWidth(32)) rom_1 ();  // open: addr, data, sel
endmodule

module Extender (
  input  [15:0] in_1,
  output [31:0] out_2
);

  assign out_2 = {{16{1'b0}}, in_1};  // Bit_Extender bit_extender_1
endmodule
